// Logisim project Trident.circ as structural Verilog: 1 circuit, main circuit main
module main (
  output [15:0] out_1,
  output [7:0] Sum,
  output [7:0] Difference
);

  wire and_1_out, and_2_out, and_3_out, and_4_out, and_5_out, decoder_1_out0, decoder_1_out1, decoder_1_out2,
       decoder_1_out3, diff, InstructClock_out, sum_t, TheClock_out;
  wire [1:0] demultiplexer_1_out1, demultiplexer_1_out2;
  wire [7:0] adder_1_out, demultiplexer_2_out1, demultiplexer_2_out2, demultiplexer_3_out1,
       demultiplexer_3_out2, multiplexer_1_out, multiplexer_2_out, PC_q, Regiser3_q, Register0_q,
       Register1_q, Register2_q;

  Adder adder_1 (.a(PC_q), .b(8'h1), .out(adder_1_out));  // open: cin, cout
  Register PC (.D(adder_1_out), .en(1'b1), .clk(InstructClock_out), .Q(PC_q));  // open: clr
  Clock InstructClock (.out(InstructClock_out));
  RAM #(.dataWidth(16), .enables("line")) ram_1 (
    .addr(PC_q), .we(1'b0), .clk(InstructClock_out), .dout(out_1));  // open: din
  and and_1 (and_1_out, out_1[14], out_1[15]);
  Decoder #(.select(2)) decoder_1 (
    .out0(decoder_1_out0), .out1(decoder_1_out1), .out2(decoder_1_out2), .out3(decoder_1_out3),
    .sel(out_1[11:10]));  // open: en
  Clock TheClock (.out(TheClock_out));
  and and_2 (and_2_out, decoder_1_out0, and_1_out);
  and and_3 (and_3_out, decoder_1_out1, and_1_out);
  and and_4 (and_4_out, decoder_1_out2, and_1_out);
  and and_5 (and_5_out, decoder_1_out3, and_1_out);
  Register Register0 (.D(out_1[7:0]), .en(and_2_out), .clk(TheClock_out), .Q(Register0_q));  // open: clr
  Register Register1 (.D(out_1[7:0]), .en(and_3_out), .clk(TheClock_out), .Q(Register1_q));  // open: clr
  Register Register2 (.D(out_1[7:0]), .en(and_4_out), .clk(TheClock_out), .Q(Register2_q));  // open: clr
  Register Regiser3 (.D(out_1[7:0]), .en(and_5_out), .clk(TheClock_out), .Q(Regiser3_q));  // open: clr
  Demultiplexer #(.select(2), .width(2)) demultiplexer_1 (
    .out1(demultiplexer_1_out1), .out2(demultiplexer_1_out2), .in(out_1[15:14]), .sel(out_1[15:14]));  // open: out0, out3
  Multiplexer #(.select(2), .width(8)) multiplexer_1 (
    .in0(Register0_q), .in1(Register1_q), .in2(Register2_q), .in3(Regiser3_q), .out(multiplexer_1_out),
    .sel(out_1[9:8]));
  Multiplexer #(.select(2), .width(8)) multiplexer_2 (
    .in0(Register0_q), .in1(Register1_q), .in2(Register2_q), .in3(Regiser3_q), .out(multiplexer_2_out),
    .sel(out_1[11:10]));
  Demultiplexer #(.select(2), .width(8)) demultiplexer_2 (
    .out1(demultiplexer_2_out1), .out2(demultiplexer_2_out2), .in(multiplexer_1_out), .sel(out_1[15:14]));  // open: out0, out3
  Demultiplexer #(.select(2), .width(8)) demultiplexer_3 (
    .out1(demultiplexer_3_out1), .out2(demultiplexer_3_out2), .in(multiplexer_2_out), .sel(out_1[15:14]));  // open: out0, out3
  BitSelector #(.width(2)) bitselector_1 (.in(demultiplexer_1_out1), .out(sum_t), .sel(1'b0));
  BitSelector #(.width(2)) bitselector_2 (.in(demultiplexer_1_out2), .out(diff), .sel(1'b1));
  LED led_1 (.in(sum_t));
  Adder adder_2 (.a(demultiplexer_3_out1), .b(demultiplexer_2_out1), .out(Sum));  // open: cin, cout
  LED led_2 (.in(sum_t));
  LED led_3 (.in(diff));
  Subtractor subtractor_1 (.a(demultiplexer_3_out2), .b(demultiplexer_2_out2), .out(Difference));  // open: bin, bout
  LED led_4 (.in(diff));
  LED led_5 (.in(sum_t));
  LED led_6 (.in(sum_t));
  LED led_7 (.in(sum_t));
  LED led_8 (.in(sum_t));
  LED led_9 (.in(diff));
  LED led_10 (.in(diff));
  LED led_11 (.in(diff));
  LED led_12 (.in(diff));
  LED led_13 (.in(sum_t));
  LED led_14 (.in(diff));

  // Other names for the same wires on the sheet: Rn[1:0] = out_1[9:8]; Rm[1:0] = out_1[11:10];
  //   opcode[1:0] = out_1[15:14]

  // Notes on the sheet:
  //   Ryan Lee
  //   I pledge my honor that I have abided by the Stevens Honor System.
  //   MemWrite
  //   Imm8
  //   WriteReg
  //   RegWrite
  //   ReadPort1
endmodule
